// Logisim project ai.circ as structural Verilog: 3 circuits, main circuit AI
module AI (
  input  reset,
  input  level,
  input  state,
  input  double_speed,
  input  [7:0] x,
  input  [7:0] y,
  output [1:0] dir_bat,
  output [4:0] batY
);

  wire _0xf1_out, _0xf2_out, _0xf3_out, _0xf4_out, and_2_out, cdm_8_mark5_1_p1, cdm_8_mark5_1_p2,
       cdm_8_mark5_1_p4, cdm_8_mark5_1_p5, cdm_8_mark5_1_p6, cdm_8_mark5_1_p7, cdm_8_mark5_1_p8,
       cdm_8_mark5_1_p9, cdm_8_mark5_1_p10, clock, code, data, decoder_1_out1, decoder_1_out2,
       decoder_1_out3, decoder_1_out4, I_Osel, not_1_out, not_2_out, RAM, rd_wr;
  wire [3:0] I_Oadr;
  wire [5:0] faults_1_baty_out;
  wire [5:5] steps_1_baty_out;
  wire [7:0] cdm_8_mark5_1_p13, cdm_8_mark5_1_p14, I_Odata, register_1_q;
  wire [7:4] cdm_8_mark5_1_p12;

  // Probe on cdm_8_mark5_1_p2
  // Probe on cdm_8_mark5_1_p1
  // Probe on cdm_8_mark5_1_p4
  and and_1 (I_Osel, and_2_out, clock, data);
  Decoder #(.select(4), .enable("false")) decoder_1 (
    .out1(decoder_1_out1), .out2(decoder_1_out2), .out3(decoder_1_out3), .out4(decoder_1_out4), .sel(I_Oadr));  // open: out0, out5, out6, out7, out8, out9, out10, out11, out12, out13, out14, out15
  // Probe on cdm_8_mark5_1_p5
  Clock clock_1 (.out(clock));
  // Probe on cdm_8_mark5_1_p7
  // Probe on cdm_8_mark5_1_p8
  // Probe on cdm_8_mark5_1_p6
  // CdM_8_mark5 cdm_8_mark5_1: pin names not known; wires that end beside it: cdm_8_mark5_1_p1, cdm_8_mark5_1_p2, clock, cdm_8_mark5_1_p4, cdm_8_mark5_1_p5, cdm_8_mark5_1_p6, cdm_8_mark5_1_p7, cdm_8_mark5_1_p8, cdm_8_mark5_1_p9, cdm_8_mark5_1_p10, rd_wr, {cdm_8_mark5_1_p12, I_Oadr}, cdm_8_mark5_1_p13, cdm_8_mark5_1_p14
  and and_2 (and_2_out, cdm_8_mark5_1_p12[4], cdm_8_mark5_1_p12[5], cdm_8_mark5_1_p12[6], cdm_8_mark5_1_p12[7]);
  Decoder #(.disabled(0)) decoder_2 (.out0(code), .out1(data), .sel(cdm_8_mark5_1_p9), .en(cdm_8_mark5_1_p10));
  assign I_Odata = not_1_out ? cdm_8_mark5_1_p13 : 8'bz;  // Controlled_Buffer controlled_buffer_1
  not not_1 (not_1_out, rd_wr);
  assign cdm_8_mark5_1_p14 = rd_wr ? I_Odata : 8'bz;  // Controlled_Buffer controlled_buffer_2
  and _0xf1 (_0xf1_out, decoder_1_out1, ~rd_wr, I_Osel);  // AND_Gate
  and _0xf2 (_0xf2_out, decoder_1_out2, rd_wr, I_Osel);
  and _0xf3 (_0xf3_out, decoder_1_out3, rd_wr, I_Osel);
  and _0xf4 (_0xf4_out, decoder_1_out4, rd_wr, I_Osel);
  and and_3 (RAM, data, not_2_out);
  not not_2 (not_2_out, I_Osel);
  Register register_1 (.D(I_Odata), .Q(register_1_q), .clk(_0xf1_out));  // open: en, clr
  assign I_Odata = _0xf2_out ? x : 8'bz;  // Controlled_Buffer controlled_buffer_3
  assign I_Odata = _0xf3_out ? y : 8'bz;  // Controlled_Buffer controlled_buffer_4
  assign I_Odata = _0xf4_out ? {{7{1'b0}}, state} : 8'bz;  // Controlled_Buffer controlled_buffer_5
  // Probe on {cdm_8_mark5_1_p12, I_Oadr}
  ROM rom_1 (.addr({cdm_8_mark5_1_p12, I_Oadr}), .data(I_Odata), .sel(code));
  RAM #(.bus("separate")) ram_1 (
    .addr({cdm_8_mark5_1_p12, I_Oadr}), .din(I_Odata), .data(I_Odata), .sel(RAM), .clk(clock), .ld(rd_wr),
    .clr(reset));  // open: str
  faults faults_1 (.batY_in(register_1_q[5:0]), .batY_out(faults_1_baty_out), .level(level));
  // Probe on I_Odata
  steps steps_1 (
    .batY_in(faults_1_baty_out), .batY_out({steps_1_baty_out[5], batY}), .dir_bat(dir_bat), .state(state),
    .double_speed(double_speed), .x(x[5:0]), .lvl(level));

  // Notes on the sheet:
  //   contents of rom_1 (hex, n*v repeats v):
  //   cd f0 d1 f4 b5 5 e1 f d2 f d0 f1 a2 ee 2 d1 f2 d2 f3 b5 ba 7 d0 1f 41 d0 20 43 f e0 4a b d0 1f 42 d0
  //   20 43 f e0 3b d0 1d 34 84 98 d3 1d 12 7e ea 39 3b d2 1d 3b b ee 48 d0 1d 34 84 98 78 ea 46 32 ee 48
  //   38 2 ee 51 d2 f d0 f1 a2 ee 2 d0 f1 a2 ee 2 d4
endmodule

module steps (
  input  state,
  input  double_speed,
  input  [5:0] batY_in,
  input  [5:0] x,
  input  lvl,
  output [5:0] batY_out,
  output [1:0] dir_bat
);

  wire and_1_out, clock_1_out, clock_4_out, clock_5_out, comparator_3_lt, comparator_4_lt, multiplexer_4_out,
       not_1_out, not_2_out, not_3_out, not_4_out, or_1_out, register_1_q;
  wire [1:0] clock_2_out;
  wire [2:0] comparator_1_gt, comparator_2_gt;
  wire [5:0] adder_1_out, controlled_buffer_1_out, controlled_buffer_2_out, controlled_buffer_4_out,
       multiplexer_1_out, multiplexer_2_out, multiplexer_3_out, subtractor_1_out;

  Comparator #(.width(6)) comparator_1 (
    .a(batY_in), .b({6{1'b0}}), .gt(comparator_1_gt[0]), .eq(comparator_1_gt[1]), .lt(comparator_1_gt[2]));
  // Probe on subtractor_1_out
  Subtractor #(.width(6)) subtractor_1 (.a(batY_in), .b(6'b000001), .out(subtractor_1_out));  // open: bin, bout
  Multiplexer #(.select(3), .width(6), .disabled(0), .enable("false")) multiplexer_1 (
    .in1(subtractor_1_out), .in2({6{1'b0}}), .in4({6{1'b0}}), .out(multiplexer_1_out), .sel(comparator_1_gt));  // open: in0, in3, in5, in6, in7
  Comparator #(.width(6)) comparator_2 (
    .a(multiplexer_1_out), .b(controlled_buffer_4_out), .gt(comparator_2_gt[0]), .eq(comparator_2_gt[1]),
    .lt(comparator_2_gt[2]));
  Adder #(.width(6)) adder_1 (
    .a(controlled_buffer_4_out), .b(multiplexer_2_out), .out(adder_1_out));  // open: cin, cout
  Multiplexer #(.select(3), .width(6), .enable("false")) multiplexer_2 (
    .in1(6'b000001), .in2({6{1'b0}}), .in4({6{1'b1}}), .out(multiplexer_2_out), .sel(comparator_2_gt));  // open: in0, in3, in5, in6, in7
  Clock #(.highDuration(26), .lowDuration(510)) clock_1 (.out(clock_1_out));
  assign controlled_buffer_1_out = not_1_out ? adder_1_out : 6'bz;  // Controlled_Buffer controlled_buffer_1
  not not_1 (not_1_out, comparator_3_lt);
  Comparator #(.width(6), .mode("unsigned")) comparator_3 (
    .a(6'b011101), .b(adder_1_out), .lt(comparator_3_lt));  // open: gt, eq
  Comparator #(.width(6), .mode("unsigned")) comparator_4 (.a(6'b111001), .b(x), .lt(comparator_4_lt));  // open: gt, eq
  not not_2 (not_2_out, comparator_4_lt);
  not not_3 (not_3_out, lvl);
  not not_4 (not_4_out, register_1_q);
  Register #(.width(1)) register_1 (.D(state), .Q(register_1_q), .clk(clock_1_out));  // open: en, clr
  Clock #(.highDuration(13), .lowDuration(13)) clock_2 (.out(clock_2_out[0]));
  Clock #(.highDuration(17), .lowDuration(17)) clock_3 (.out(clock_2_out[1]));
  Multiplexer #(.width(6), .enable("false")) multiplexer_3 (
    .in0(6'b001110), .in1(controlled_buffer_2_out), .out(multiplexer_3_out), .sel(state));
  assign controlled_buffer_2_out = or_1_out ? controlled_buffer_1_out : 6'bz;  // Controlled_Buffer controlled_buffer_2
  Register #(.width(6)) register_2 (.D(multiplexer_3_out), .Q(batY_out), .clk(multiplexer_4_out));  // open: en, clr
  Multiplexer #(.disabled(0), .enable("false")) multiplexer_4 (
    .in0(clock_4_out), .in1(clock_5_out), .out(multiplexer_4_out), .sel(double_speed));
  Clock #(.highDuration(15), .lowDuration(15)) clock_4 (.out(clock_4_out));
  Clock #(.highDuration(9), .lowDuration(9)) clock_5 (.out(clock_5_out));
  or or_1 (or_1_out, and_1_out, lvl);
  and and_1 (and_1_out, not_2_out, not_3_out);
  assign dir_bat = not_4_out ? clock_2_out : 2'bz;  // Controlled_Buffer controlled_buffer_3
  Pull_Resistor pull_resistor_1 (.node(dir_bat));
  assign controlled_buffer_4_out = state ? batY_out : 6'bz;  // Controlled_Buffer controlled_buffer_4

  // Notes on the sheet:
  //   random
endmodule

module faults (
  input  [5:0] batY_in,
  input  level,
  output [5:0] batY_out
);

  wire clock_1_out, clock_2_out, comparator_1_gt;
  wire [2:0] multiplexer_1_out, random_2_out;
  wire [3:0] random_1_out;
  wire [5:0] adder_1_out, bit_extender_1_out;

  Clock #(.highDuration(100), .lowDuration(100)) clock_1 (.out(clock_1_out));
  Random #(.width(4)) random_1 (.clk(clock_1_out), .next(1'b1), .out(random_1_out));  // open: clr
  Clock #(.highDuration(100), .lowDuration(100)) clock_2 (.out(clock_2_out));
  Random #(.width(3)) random_2 (.clk(clock_2_out), .next(1'b1), .out(random_2_out));  // open: clr
  Comparator #(.width(4)) comparator_1 (.a(random_1_out), .b(4'b0000), .gt(comparator_1_gt));  // open: eq, lt
  assign bit_extender_1_out = {{3{1'b0}}, multiplexer_1_out};  // Bit_Extender bit_extender_1
  Multiplexer #(.width(3), .disabled(0), .enable("false")) multiplexer_1 (
    .in0(random_2_out), .in1(3'b000), .out(multiplexer_1_out), .sel(comparator_1_gt));
  Adder #(.width(6)) adder_1 (.a(bit_extender_1_out), .b(batY_in), .out(adder_1_out));  // open: cin, cout
  Multiplexer #(.width(6), .disabled(0), .enable("false")) multiplexer_2 (
    .in0(adder_1_out), .in1(batY_in), .out(batY_out), .sel(level));
endmodule
